# Fritzing sketch servo_firebettle (saved by Fritzing 0.9.9b)
breadboards: 1

parts:
  M1 = ESP32 FIREBEETLE IOT V3 [part_number=ESP32_FIREBEETLE]
  Power_plug1 = Power plug
  J1 = Basic Servo

nets:
  GND: M1.GND, Power_plug1.GND, J1.gnd
  VCC: M1.VCC, M1.LIPO+, Power_plug1.VCC, J1.vcc

notes:
  +5V

custom parts:
  ESP32 FIREBEETLE IOT V3: DFRobot Firebeetle ESP32 IOT Microcontroller V3, 36-Pin ESP32.
